# Fritzing sketch Hardware (saved by Fritzing 0.9.1b)
breadboards: 1

parts:
  Part1 = Arduino Uno (Rev3)
  LCD1 = LCD screen
  Part2 = Bluetooth HC-05 Macho

nets:
  N1: Part1.D9_PWM, LCD1.LED+
  N2: Part1.D11_PWM/MOSI, LCD1.E
  N3: Part1.D12/MISO, LCD1.RS
  N4: Part1.D2, LCD1.DB7
  N5: Part1.D3_PWM, LCD1.DB6
  N6: Part1.D4, LCD1.DB5
  N7: Part1.D5_PWM, LCD1.DB4
  N8: Part1.D6_PWM, Part2.TXD
  N9: Part1.D7, Part2.RXD
  5V: Part1.5V, LCD1.VDD, Part2.VCC
  GND: Part1.GND, LCD1.VSS, LCD1.V0, LCD1.R/W, LCD1.LED-, Part2.GND
